# Fritzing sketch diagrama-esquematico-Gerador-Frequencias-Arduino (saved by Fritzing 0.9.2b)

parts:
  S1 = Pushbutton [package="[THT]"]
  S2 = Pushbutton [package="[THT]"]
  S3 = Pushbutton [package="[THT]"]
  S4 = Pushbutton [package="[THT]"]
  S5 = Pushbutton [package="[THT]"]
  S6 = Pushbutton [package="[THT]"]
  S7 = Pushbutton [package="[THT]"]
  S8 = Pushbutton [package="[THT]"]
  S9 = Pushbutton [package="[THT]"]
  S10 = Pushbutton [package="[THT]"]
  R1 = Resistor [tolerance=±5% resistance=8.2k package="0402 [SMD]"]
  R2 = Resistor [tolerance=±5% resistance=10k package="0402 [SMD]"]
  R3 = Resistor [tolerance=±5% resistance=12k package="0402 [SMD]"]
  R4 = Resistor [tolerance=±5% resistance=33k package="0402 [SMD]"]
  R5 = Resistor [tolerance=±5% resistance=39k package="0402 [SMD]"]
  R6 = Resistor [tolerance=±5% resistance=22k package="0402 [SMD]"]
  R7 = Resistor [tolerance=±5% resistance=56k package="0402 [SMD]"]
  R8 = Resistor [tolerance=±5% resistance=68k package="0402 [SMD]"]
  R9 = Resistor [tolerance=±5% resistance=47k package="0402 [SMD]"]
  R10 = Resistor [tolerance=±5% resistance=100k package="0402 [SMD]"]
  R11 = Resistor [tolerance=±5% resistance=10k package="0402 [SMD]"]
  Componente1 = Arduino Uno (Rev3) - ICSP
  J1 = Piezo Speaker
  R12 = Resistor [tolerance=±5% resistance=1k package="0402 [SMD]"]

nets:
  N1: S1.Pin_1, S1.Pin_2, R9.Pin_0
  N2: S1.Pin_4, S2.Pin_4, S3.Pin_3, S3.Pin_4, S4.Pin_4, S5.Pin_3, S5.Pin_4, S6.Pin_4, S7.Pin_3, S7.Pin_4, S9.Pin_4, R11.Pin_1, Componente1.A0
  N3: S2.Pin_1, S2.Pin_2, R7.Pin_0
  N4: S3.Pin_1, S3.Pin_2, R8.Pin_0
  N5: S4.Pin_1, S4.Pin_2, R5.Pin_0
  N6: S5.Pin_1, S5.Pin_2, R6.Pin_0
  N7: S6.Pin_1, S6.Pin_2, R4.Pin_0
  N8: S7.Pin_1, S7.Pin_2, R3.Pin_0
  N9: S8.Pin_1, S8.Pin_2, R1.Pin_0
  N10: S9.Pin_2, R2.Pin_0
  N11: S10.Pin_1, S10.Pin_2, R10.Pin_0
  N12: R1.Pin_1, R10.Pin_1, Componente1.GND, J1.pin1
  N13: R11.Pin_0, Componente1.5V
  N14: Componente1.D10_PWM/SS, R12.Pin_1

notes:
  +5V
  GND
  Entrada Analógica
  A0
  1
  5
  10
